// Logisim project ALU.circ as structural Verilog: 1 circuit, main circuit main
module main (
  input  A3,
  input  A2,
  input  A1,
  input  A0,
  input  CS2,
  input  CS1,
  input  CS0,
  input  B3,
  input  B2,
  input  B1,
  input  B0,
  output Out_3,
  output Out_2,
  output Out_1,
  output Out_0,
  output out_16,
  output Z,
  output S,
  output C,
  output V
);

  wire n7404_1_p1, n7404_1_p3, n7404_1_p4, n7404_1_p7, n7404_1_p11, n7404_1_p13, n7404_1_p15, n7408_1_p6,
       n7408_1_p9, n7408_1_p14, n7408_1_p17, n7408_2_p3, n7408_2_p6, n7408_2_p9, n7408_2_p10, n7408_3_p3,
       n7408_3_p10, n7408_3_p11, n7408_3_p12, n7408_3_p14, n7432_1_p3, n7432_1_p6, n7432_1_p10, n7486_1_p4,
       n7486_1_p7, n7486_1_p13, n7486_2_p3, n7486_2_p6, n7486_2_p11, n7486_2_p14, n74157_1_p4, n74157_1_p7,
       n74157_1_p13, n74157_1_p16, n74157_2_p4, n74157_2_p7, n74157_2_p13, n74157_2_p16;

  // _7404 7404_1: pin names not known; wires that end beside it: n7404_1_p1, CS2, n7404_1_p3, n7404_1_p4, Z, CS0, n7404_1_p7, 1'b0, 1'b1, B3, n7404_1_p11, B2, n7404_1_p13, B1, n7404_1_p15
  // _7408 7408_1: pin names not known; wires that end beside it: CS1, n7404_1_p1, CS0, n7404_1_p7, CS1, n7408_1_p6, n7408_1_p6, n7404_1_p3, n7408_1_p9, 1'b0, 1'b1, CS2, CS1, n7408_1_p14, n7408_1_p14, n7404_1_p7, n7408_1_p17
  // _7408 7408_2: pin names not known; wires that end beside it: CS1, CS0, n7408_2_p3, n7408_2_p3, CS2, n7408_2_p6, 1'b0, 1'b1, n7408_2_p9, n7408_2_p10, V, 1'b1
  // _7486 7486_1: pin names not known; wires that end beside it: 1'b0, B0, 1'b1, n7486_1_p4, CS0, CS1, n7486_1_p7, 1'b0, n7408_2_p6, 1'b1, n7408_2_p10, out_16, n7486_1_p13, n7408_2_p9
  // _7432 7432_1: pin names not known; wires that end beside it: n7408_2_p3, n7408_1_p14, n7432_1_p3, Out_0, Out_1, n7432_1_p6, 1'b1, Out_2, Out_3, n7432_1_p10, n7432_1_p10, n7432_1_p6, n7404_1_p4
  // _7486 7486_2: pin names not known; wires that end beside it: n7408_1_p9, A0, n7486_2_p3, n7408_1_p9, A1, n7486_2_p6, 1'b0, 1'b1, n7408_1_p9, A3, n7486_2_p11, A2, n7408_1_p9, n7486_2_p14
  // _74157 74157_1: pin names not known; wires that end beside it: n7408_1_p17, B3, n7404_1_p11, n74157_1_p4, B2, n7404_1_p13, n74157_1_p7, 1'b0, 1'b1, 1'b0, B0, n7486_1_p4, n74157_1_p13, B1, n7404_1_p15, n74157_1_p16
  // _74157 74157_2: pin names not known; wires that end beside it: n7432_1_p3, n7408_1_p17, n74157_1_p4, n74157_2_p4, n7408_1_p17, n74157_1_p7, n74157_2_p7, 1'b0, 1'b1, 1'b0, n7408_1_p17, n74157_1_p13, n74157_2_p13, n7408_1_p17, n74157_1_p16, n74157_2_p16
  // _7408 7408_3: pin names not known; wires that end beside it: n7486_1_p13, n7408_2_p10, n7408_3_p3, n7408_2_p10, out_16, C, 1'b0, 1'b1, n7408_2_p10, n7408_3_p10, n7408_3_p11, n7408_3_p12, n7408_2_p10, n7408_3_p14
  // adderseparate_main main_1: pin names not known; wires that end beside it: n74157_2_p4, n7408_3_p3, 1'b1, 1'b1, n7486_1_p13, 1'b0, 1'b0, n7486_2_p11, Out_3, out_16, n7408_3_p11, 1'b0, n74157_2_p7, n7486_2_p14, Out_2
  // adderseparate_main main_2: pin names not known; wires that end beside it: n74157_2_p16, n7408_3_p14, 1'b1, 1'b1, n7408_3_p12, 1'b0, 1'b0, n7486_2_p6, Out_1, n7408_3_p10, n7486_1_p7, 1'b0, n74157_2_p13, n7486_2_p3, Out_0, n7408_3_p12

  assign S = Out_3;

  // Notes on the sheet:
  //   2
  //   1
  //   S1
  //   S2
  //   3
  //   A3
  //   A2
  //   A1
  //   A0
  //   B3
  //   B2
  //   B1
  //   B0
endmodule
